# Fritzing sketch AES_PCB (saved by Fritzing 0.9.4)
breadboards: 1

parts:
  Part1 = Arduino Mega 2560 (Rev3)
  S1 = Pushbutton [package="[THT]"]
  S2 = Pushbutton [package="[THT]"]
  S3 = Pushbutton [package="[THT]"]
  S4 = Pushbutton [package="[THT]"]
  R1 = Resistor [tolerance=±5% resistance=10k package=THT]
  R4 = Resistor [tolerance=±5% resistance=10k package=THT]
  R5 = Resistor [tolerance=±5% resistance=10k package=THT]
  R6 = Resistor [tolerance=±5% resistance=10k package=THT]
  Part2 = Thumb Joystick
  DFRobot_DFPlayer_Mini1 = DFRobot DFPlayer Mini [part_number=DFR0299]
  SP1 = SPEAKER [package=pcb_mount_speaker]
  R8 = Resistor [tolerance=±5% resistance=1k package=THT]
  R9 = Rotary Potentiometer (Small) [maximum_resistance=100kΩ package=THT]
  U1 = M10X2 [package=2x10_lock]
  U2 = M10X2 [package=2x10_lock]
  JP1 = Header 10 [package=1x10-2mm-smd]

nets:
  N1: Part1.A0, Part2.HORZ
  N2: Part1.A1, Part2.VERT
  N3: Part1.A2, R9.wiper
  GND: Part1.GND, R1.Pin_1, R4.Pin_1, R6.Pin_1, Part2.GND, DFRobot_DFPlayer_Mini1.GND-1, DFRobot_DFPlayer_Mini1.GND-2, R9.leg1, U1.15, U1.16
  N4: Part1.D13_PWM, DFRobot_DFPlayer_Mini1.TX
  N5: Part1.D12_PWM, R8.Pin_1
  N6: Part1.D11_PWM, S1.Pin_1, S1.Pin_2, R1.Pin_0
  N7: Part1.D10_PWM, S2.Pin_1, S2.Pin_2, R4.Pin_0
  N8: Part1.D9_PWM, S3.Pin_1, S3.Pin_2, R5.Pin_0
  N9: Part1.D8_PWM, S4.Pin_1, S4.Pin_2, R6.Pin_0
  VCC: Part1.5V, S1.Pin_3, S1.Pin_4, S2.Pin_3, S2.Pin_4, S3.Pin_3, S3.Pin_4, S4.Pin_3, S4.Pin_4, Part2.VCC, DFRobot_DFPlayer_Mini1.VCC, R9.leg2, U2.1, U2.2
  N10: Part1.D0_RX0, JP1.8
  N11: Part1.D1_TX0, JP1.7
  N12: Part1.D2_PWM, JP1.6
  N13: Part1.D3_PWM, JP1.5
  N14: Part1.D4_PWM, JP1.4
  N15: Part1.D5_PWM, JP1.3
  N16: Part1.D6_PWM, JP1.2
  N17: Part1.D7_PWM, JP1.1
  N18: Part1.D22, U2.3
  N19: Part1.D23, U2.4
  N20: Part1.D24, U2.5
  N21: Part1.D25, U2.6
  N22: Part1.D26, U2.7
  N23: Part1.D27, U2.8
  N24: Part1.D28, U2.9
  N25: Part1.D29, U2.10
  N26: Part1.D30, U2.11
  N27: Part1.D31, U2.12
  N28: Part1.D32, U2.13
  N29: Part1.D33, U2.14
  N30: Part1.D34, U2.15
  N31: Part1.D35, U2.16
  N32: Part1.D36, U2.17
  N33: Part1.D37, U2.18
  N34: Part1.D38, U2.19
  N35: Part1.D39, U2.20
  N36: Part1.D40, U1.1
  N37: Part1.D41, U1.2
  N38: Part1.D42, U1.3
  N39: Part1.D43, U1.4
  N40: Part1.D44, U1.5
  N41: Part1.D45, U1.6
  N42: Part1.D46, U1.7
  N43: Part1.D47, U1.8
  N44: Part1.D48, U1.9
  N45: Part1.D49, U1.10
  N46: Part1.D50, U1.11
  N47: Part1.D51, U1.12
  N48: Part1.D52, U1.13
  N49: Part1.D53, U1.14
  N50: DFRobot_DFPlayer_Mini1.RX, R8.Pin_0
  N51: DFRobot_DFPlayer_Mini1.SPK_1, SP1.+
  N52: DFRobot_DFPlayer_Mini1.SPK_2, SP1.-
